# Fritzing sketch MMJoy2.f (AT90USB1286-Teensy++2.0, USB2.0) (saved by Fritzing 0.9.0b)

parts:
  Teensy++1 = Teensy++ 2.0
  Linear_Potentiometer_10k-100k = POT [package=alps_pot]
  C1 = Ceramic Capacitor [capacitance=0.1µF package="0805 [SMD, multilayer]"]  # not connected
  Linear_Pot_10k-100k1 = POT [package=alps_pot]
  Linear_Pot_10k-100k2 = POT [package=alps_pot]
  Linear_Pot_10k-100k3 = POT [package=alps_pot]
  Linear_Pot_10k-100k4 = POT [package=alps_pot]
  Linear_Pot_10k-100k5 = POT [package=alps_pot]
  Linear_Pot_10k-100k6 = POT [package=alps_pot]
  Linear_Pot_10k-100k7 = POT [package=alps_pot]
  S48 = Pushbutton [package="[THT]"]
  S49 = Pushbutton [package="[THT]"]
  S50 = Pushbutton [package="[THT]"]
  S51 = Pushbutton [package="[THT]"]
  S52 = Pushbutton [package="[THT]"]
  S53 = Pushbutton [package="[THT]"]
  S54 = Pushbutton [package="[THT]"]
  S55 = Pushbutton [package="[THT]"]
  S56 = Pushbutton [package="[THT]"]
  S57 = Pushbutton [package="[THT]"]
  S58 = Pushbutton [package="[THT]"]
  S59 = Pushbutton [package="[THT]"]
  S60 = Pushbutton [package="[THT]"]
  S61 = Pushbutton [package="[THT]"]
  S62 = Pushbutton [package="[THT]"]
  S63 = Pushbutton [package="[THT]"]
  S64 = Pushbutton [package="[THT]"]
  S65 = Pushbutton [package="[THT]"]
  S66 = Pushbutton [package="[THT]"]
  S67 = Pushbutton [package="[THT]"]
  S68 = Pushbutton [package="[THT]"]
  S69 = Pushbutton [package="[THT]"]
  S70 = Pushbutton [package="[THT]"]
  S71 = Pushbutton [package="[THT]"]
  S72 = Pushbutton [package="[THT]"]
  S73 = Pushbutton [package="[THT]"]
  S74 = Pushbutton [package="[THT]"]
  S75 = Pushbutton [package="[THT]"]
  S76 = Pushbutton [package="[THT]"]
  S77 = Pushbutton [package="[THT]"]
  S78 = Pushbutton [package="[THT]"]
  S79 = Pushbutton [package="[THT]"]
  D44 = Diode [package=diode-1n4148]
  D45 = Diode [package=diode-1n4148]
  D46 = Diode [package=diode-1n4148]
  D47 = Diode [package=diode-1n4148]
  D48 = Diode [package=diode-1n4148]  # not connected
  D49 = Diode [package=diode-1n4148]
  D50 = Diode [package=diode-1n4148]
  D51 = Diode [package=diode-1n4148]
  D52 = Diode [package=diode-1n4148]  # not connected
  D53 = Diode [package=diode-1n4148]  # not connected
  D54 = Diode [package=diode-1n4148]
  D55 = Diode [package=diode-1n4148]
  D56 = Diode [package=diode-1n4148]
  D57 = Diode [package=diode-1n4148]
  D58 = Diode [package=diode-1n4148]  # not connected
  D59 = Diode [package=diode-1n4148]
  D60 = Diode [package=diode-1n4148]  # not connected
  D61 = Diode [package=diode-1n4148]  # not connected
  D62 = Diode [package=diode-1n4148]  # not connected
  D63 = Diode [package=diode-1n4148]  # not connected
  D64 = Diode [package=diode-1n4148]
  D65 = Diode [package=diode-1n4148]
  D66 = Diode [package=diode-1n4148]
  D67 = Diode [package=diode-1n4148]
  D68 = Diode [package=diode-1n4148]
  D69 = Diode [package=diode-1n4148]
  D70 = Diode [package=diode-1n4148]  # not connected
  D71 = Diode [package=diode-1n4148]
  D72 = Diode [package=diode-1n4148]
  D73 = Diode [package=diode-1n4148]
  D74 = Diode [package=diode-1n4148]
  D75 = Diode [package=diode-1n4148]
  S80 = Pushbutton [package="[THT]"]
  S81 = Pushbutton [package="[THT]"]
  S82 = Pushbutton [package="[THT]"]
  S83 = Pushbutton [package="[THT]"]
  S84 = Pushbutton [package="[THT]"]
  S85 = Pushbutton [package="[THT]"]
  S86 = Pushbutton [package="[THT]"]
  S87 = Pushbutton [package="[THT]"]
  S88 = Pushbutton [package="[THT]"]
  S89 = Pushbutton [package="[THT]"]
  S90 = Pushbutton [package="[THT]"]
  S91 = Pushbutton [package="[THT]"]
  S92 = Pushbutton [package="[THT]"]
  S93 = Pushbutton [package="[THT]"]
  S94 = Pushbutton [package="[THT]"]
  S95 = Pushbutton [package="[THT]"]
  S96 = Pushbutton [package="[THT]"]
  S97 = Pushbutton [package="[THT]"]
  S98 = Pushbutton [package="[THT]"]
  S99 = Pushbutton [package="[THT]"]
  S100 = Pushbutton [package="[THT]"]
  S101 = Pushbutton [package="[THT]"]
  S102 = Pushbutton [package="[THT]"]
  S103 = Pushbutton [package="[THT]"]
  S104 = Pushbutton [package="[THT]"]
  S105 = Pushbutton [package="[THT]"]
  S106 = Pushbutton [package="[THT]"]
  S107 = Pushbutton [package="[THT]"]
  S108 = Pushbutton [package="[THT]"]
  S109 = Pushbutton [package="[THT]"]
  S110 = Pushbutton [package="[THT]"]
  S111 = Pushbutton [package="[THT]"]
  D76 = Diode [package=diode-1n4148]
  D77 = Diode [package=diode-1n4148]
  D78 = Diode [package=diode-1n4148]
  D79 = Diode [package=diode-1n4148]
  D80 = Diode [package=diode-1n4148]
  D81 = Diode [package=diode-1n4148]
  D82 = Diode [package=diode-1n4148]
  D83 = Diode [package=diode-1n4148]
  D84 = Diode [package=diode-1n4148]
  D85 = Diode [package=diode-1n4148]
  D86 = Diode [package=diode-1n4148]
  D87 = Diode [package=diode-1n4148]
  D88 = Diode [package=diode-1n4148]
  D89 = Diode [package=diode-1n4148]
  D90 = Diode [package=diode-1n4148]
  D91 = Diode [package=diode-1n4148]
  D92 = Diode [package=diode-1n4148]
  D93 = Diode [package=diode-1n4148]
  D94 = Diode [package=diode-1n4148]
  D95 = Diode [package=diode-1n4148]
  D96 = Diode [package=diode-1n4148]
  D97 = Diode [package=diode-1n4148]
  D98 = Diode [package=diode-1n4148]
  D99 = Diode [package=diode-1n4148]
  D100 = Diode [package=diode-1n4148]
  D101 = Diode [package=diode-1n4148]
  D102 = Diode [package=diode-1n4148]
  D103 = Diode [package=diode-1n4148]
  D104 = Diode [package=diode-1n4148]
  D105 = Diode [package=diode-1n4148]
  D106 = Diode [package=diode-1n4148]
  D107 = Diode [package=diode-1n4148]

nets:
  N1: Teensy++1.GND, Linear_Potentiometer_10k-100k.A, Linear_Pot_10k-100k7.A
  N2: Teensy++1.F7, Linear_Pot_10k-100k7.S
  N3: Teensy++1.F6, Linear_Pot_10k-100k6.S
  N4: Teensy++1.F5, Linear_Pot_10k-100k5.S
  N5: Teensy++1.F4, Linear_Pot_10k-100k4.S
  N6: Teensy++1.F3, Linear_Pot_10k-100k3.S
  N7: Teensy++1.F2, Linear_Pot_10k-100k2.S
  N8: Teensy++1.F1, Linear_Pot_10k-100k1.S
  N9: Teensy++1.F0, Linear_Potentiometer_10k-100k.S
  N10: Teensy++1.VCC, Linear_Potentiometer_10k-100k.E, Linear_Pot_10k-100k7.E
  N11: S48.Pin_3, S48.Pin_4
  N12: S49.Pin_3, S49.Pin_4
  N13: S50.Pin_3, S50.Pin_4
  N14: S51.Pin_3, S51.Pin_4
  N15: S52.Pin_3, S52.Pin_4
  N16: S53.Pin_3, S53.Pin_4
  N17: S54.Pin_3, S54.Pin_4
  N18: S55.Pin_3, S55.Pin_4
  N19: S56.Pin_3, S56.Pin_4
  N20: S57.Pin_3, S57.Pin_4
  N21: S58.Pin_3, S58.Pin_4
  N22: S59.Pin_3, S59.Pin_4
  N23: S60.Pin_3, S60.Pin_4
  N24: S61.Pin_3, S61.Pin_4
  N25: S62.Pin_3, S62.Pin_4
  N26: S63.Pin_3, S63.Pin_4
  N27: S64.Pin_3, S64.Pin_4
  N28: S65.Pin_3, S65.Pin_4
  N29: S66.Pin_3, S66.Pin_4
  N30: S67.Pin_3, S67.Pin_4
  N31: S68.Pin_3, S68.Pin_4
  N32: S69.Pin_3, S69.Pin_4
  N33: S70.Pin_3, S70.Pin_4
  N34: S71.Pin_3, S71.Pin_4
  N35: S72.Pin_3, S72.Pin_4
  N36: S73.Pin_3, S73.Pin_4
  N37: S74.Pin_3, S74.Pin_4
  N38: S75.Pin_3, S75.Pin_4
  N39: S76.Pin_3, S76.Pin_4
  N40: S77.Pin_3, S77.Pin_4
  N41: S78.Pin_3, S78.Pin_4
  N42: S79.Pin_3, S79.Pin_4
  N43: D44.C, D75.C
  N44: D45.C, D64.C, D72.C
  N45: D46.C, D51.C
  N46: D47.C, D68.C, D69.C
  N47: D49.C, D66.C
  N48: D50.C, D71.C
  N49: D54.C, D55.C, D57.C
  N50: D56.C, D73.C
  N51: D59.C, D67.C
  N52: D65.C, D74.C
  N53: S80.Pin_1, S80.Pin_3, S80.Pin_4
  N54: S81.Pin_1, S81.Pin_3, S81.Pin_4
  N55: S82.Pin_3, S82.Pin_4
  N56: S83.Pin_1, S83.Pin_3, S83.Pin_4
  N57: S84.Pin_1, S84.Pin_3, S84.Pin_4
  N58: S85.Pin_1, S85.Pin_3, S85.Pin_4
  N59: S86.Pin_1, S86.Pin_3, S86.Pin_4
  N60: S87.Pin_3, S87.Pin_4
  N61: S88.Pin_1, S88.Pin_3, S88.Pin_4
  N62: S89.Pin_1, S89.Pin_3, S89.Pin_4
  N63: S90.Pin_1, S90.Pin_3, S90.Pin_4
  N64: S91.Pin_3, S91.Pin_4
  N65: S92.Pin_3, S92.Pin_4
  N66: S93.Pin_1, S93.Pin_3, S93.Pin_4
  N67: S94.Pin_1, S94.Pin_3, S94.Pin_4
  N68: S95.Pin_1, S95.Pin_3, S95.Pin_4
  N69: S96.Pin_3, S96.Pin_4
  N70: S97.Pin_1, S97.Pin_3, S97.Pin_4
  N71: S98.Pin_3, S98.Pin_4
  N72: S99.Pin_3, S99.Pin_4
  N73: S100.Pin_3, S100.Pin_4
  N74: S101.Pin_3, S101.Pin_4
  N75: S102.Pin_3, S102.Pin_4
  N76: S103.Pin_1, S103.Pin_3, S103.Pin_4
  N77: S104.Pin_1, S104.Pin_3, S104.Pin_4
  N78: S105.Pin_1, S105.Pin_3, S105.Pin_4
  N79: S106.Pin_1, S106.Pin_3, S106.Pin_4
  N80: S107.Pin_3, S107.Pin_4
  N81: S108.Pin_1, S108.Pin_3, S108.Pin_4
  N82: S109.Pin_1, S109.Pin_3, S109.Pin_4
  N83: S110.Pin_1, S110.Pin_3, S110.Pin_4
  N84: S111.Pin_3, S111.Pin_4
  N85: D76.C, D78.C, D83.C, D85.C, D91.C, D95.C, D99.C, D107.C
  N86: D77.C, D88.C, D92.C, D93.C, D94.C, D96.C, D104.C, D105.C
  N87: D79.C, D81.C, D97.C, D98.C, D100.C, D101.C, D102.C, D106.C
  N88: D80.C, D82.C, D84.C, D86.C, D87.C, D89.C, D90.C, D103.C
