# Fritzing sketch Pins_Common (saved by Fritzing 0.9.0b)

parts:
  U3 = mystery part, 3 pins [chip_label=SS495]  # not connected
  U4 = POT [package=alps_pot]  # not connected
  S78 = Pushbutton [package="[THT]"]
  RE1 = Rotary Encoder [package=THT]
  D72 = Diode [package=diode-1n4148]
  D73 = Diode [package=diode-1n4148]
  S80 = Pushbutton [package="[THT]"]
  D75 = Diode [package=diode-1n4148]
  S81 = Pushbutton [package="[THT]"]
  D76 = Diode [package=diode-1n4148]
  S82 = Pushbutton [package="[THT]"]
  D77 = Diode [package=diode-1n4148]
  S83 = Pushbutton [package="[THT]"]
  D78 = Diode [package=diode-1n4148]
  S84 = Pushbutton [package="[THT]"]
  D79 = Diode [package=diode-1n4148]
  S85 = Pushbutton [package="[THT]"]
  D80 = Diode [package=diode-1n4148]
  S86 = Pushbutton [package="[THT]"]
  S87 = Pushbutton [package="[THT]"]
  S88 = Pushbutton [package="[THT]"]
  D81 = Diode [package=diode-1n4148]
  D82 = Diode [package=diode-1n4148]
  D83 = Diode [package=diode-1n4148]
  S89 = Pushbutton [package="[THT]"]
  S90 = Pushbutton [package="[THT]"]
  S91 = Pushbutton [package="[THT]"]
  D84 = Diode [package=diode-1n4148]
  D85 = Diode [package=diode-1n4148]
  D86 = Diode [package=diode-1n4148]
  D71 = Diode [package=diode-1n4148]
  Pro_Micro2 = Pro Micro
  U5 = POT [package=alps_pot]

nets:
  N1: S78.Pin_3, S78.Pin_4, D71.A
  N2: RE1.EncoderPinA, D72.C
  N3: RE1.EncoderPinB, D73.C
  N4: S80.Pin_3, S80.Pin_4, D75.A
  N5: S81.Pin_3, S81.Pin_4, D76.A
  N6: S82.Pin_3, S82.Pin_4, D77.A
  N7: S83.Pin_3, S83.Pin_4, D78.A
  N8: S84.Pin_3, S84.Pin_4, D79.A
  N9: S85.Pin_3, S85.Pin_4, D80.A
  N10: S86.Pin_3, S86.Pin_4, D82.A
  N11: S87.Pin_3, S87.Pin_4, D81.A
  N12: S88.Pin_3, S88.Pin_4, D83.A
  N13: S89.Pin_3, S89.Pin_4, D85.A
  N14: S90.Pin_3, S90.Pin_4, D84.A
  N15: S91.Pin_3, S91.Pin_4, D86.A
  N16: Pro_Micro2.D10, U5.S
  N17: Pro_Micro2.VCC, U5.A
  N18: Pro_Micro2.GND, U5.E

notes:
  MMJoy2 common:
  GROUND
  POWER
  MMJoy2 (c) mega_mozg.
  FREE. PERSONAL DIY ONLY. NOT FOR COMMERCIAL.
  Axis Pin / A[xx]
  Linear pot (10k-100k)
  Hall sensor
  (as sample Honeywell SS495A)
  ===AXIS===
  ===BUTTONS===
  Button matrix Columns / B[xx]
  Button matrix Rows / B[xx]
  A
  C
  B
  to next row
  to next column
  Sample, 6 buttons, 6 columns + 1 row:
  Sample, 6 buttons, 3 columns + 2 rows:
  ===ENCODERS===
  [B5] AI/AE/BM
  [B4] AI/AE/BM
  [E6] --/AE/BM
  [D7] AI/AE/BM
  [C6] --/AE/BM
  [D4] AI/AE/BM
  [D0] --/AE/BM
  [D1] --/AE/BM
  [D2] --/AE/BM
  [D3] --/AE/BM
  [B6] AI/AE/BM
  [B2] --/AE/BM/SPI-MOSI
  [B1] --/AE/BM/SPI-SCK
  [B3] --/AE/BM/SPI-MISO
  [F7] AI/AE/BM
  [F6] AI/AE/BM
  [F5] AI/AE/BM
  [F4] AI/AE/BM
  POWER (raw from USB)
  Sparkfun Pro-Micro pinout for MMJoy2:
  Axis Pin / AI[xx]

custom parts:
  Pro Micro: The SparkFun Pro Micro is a complete USB-based microcontoller development system, in a very small footprint, capable of implementing many types of projects. All programming can be done via the USB port.
